// Logisim project nand2tetris.circ as structural Verilog
module Not (
  input  Input,
  output Output
);

  nand nand_1 (Output, Input, Input);
endmodule

module And (
  input  in_1,
  input  in_2,
  output out_3
);

  wire nand_1_out;

  nand nand_1 (nand_1_out, in_1, in_2);
  Not not_1 (.Input(nand_1_out), .Output(out_3));
endmodule

module Or (
  input  a,
  input  b,
  output out_3
);

  wire not_1_output, not_2_output;

  Not not_1 (.Input(a), .Output(not_1_output));
  Not not_2 (.Input(b), .Output(not_2_output));
  nand nand_1 (out_3, not_1_output, not_2_output);
endmodule

module Xor (
  input  a,
  input  b,
  output out_3
);

  wire nand_1_out, nand_2_out, not_1_output, not_2_output;

  Not not_1 (.Input(a), .Output(not_1_output));
  Not not_2 (.Input(b), .Output(not_2_output));
  nand nand_1 (nand_1_out, not_1_output, b);
  nand nand_2 (nand_2_out, a, not_2_output);
  nand nand_3 (out_3, nand_1_out, nand_2_out);
endmodule

module Mux (
  input  sel,
  input  a,
  input  b,
  output out
);

  wire and_1_out_3, and_2_out_3, not_1_output;

  Not not_1 (.Input(sel), .Output(not_1_output));
  And and_1 (.in_1(not_1_output), .in_2(a), .out_3(and_1_out_3));
  And and_2 (.in_1(sel), .in_2(b), .out_3(and_2_out_3));
  Or or_1 (.a(and_1_out_3), .b(and_2_out_3), .out_3(out));
endmodule

module Dmux (
  input  sel,
  input  in,
  output a,
  output b
);

  wire not_1_output;

  Not not_1 (.Input(sel), .Output(not_1_output));
  And and_1 (.in_1(not_1_output), .in_2(in), .out_3(a));
  And and_2 (.in_1(sel), .in_2(in), .out_3(b));

  // Notes on the sheet:
  //   if(sel) a = in b = 0
  //   if(!sel) a = 0 b = in
endmodule

module Not16 (
  input  [15:0] in16,
  output [15:0] out16
);

  Not not_1 (.Input(in16[0]), .Output(out16[0]));
  Not not_2 (.Input(in16[1]), .Output(out16[1]));
  Not not_3 (.Input(in16[2]), .Output(out16[2]));
  Not not_4 (.Input(in16[3]), .Output(out16[3]));
  Not not_5 (.Input(in16[4]), .Output(out16[4]));
  Not not_6 (.Input(in16[5]), .Output(out16[5]));
  Not not_7 (.Input(in16[6]), .Output(out16[6]));
  Not not_8 (.Input(in16[7]), .Output(out16[7]));
  Not not_9 (.Input(in16[8]), .Output(out16[8]));
  Not not_10 (.Input(in16[9]), .Output(out16[9]));
  Not not_11 (.Input(in16[10]), .Output(out16[10]));
  Not not_12 (.Input(in16[11]), .Output(out16[11]));
  Not not_13 (.Input(in16[12]), .Output(out16[12]));
  Not not_14 (.Input(in16[13]), .Output(out16[13]));
  Not not_15 (.Input(in16[14]), .Output(out16[14]));
  Not not_16 (.Input(in16[15]), .Output(out16[15]));
endmodule
